// Logisim project Single_Cycle_CPU.circ as structural Verilog: 1 circuit, main circuit main
module main (
);

  wire and_1_out, Clk, clock_1_out, ExRegWrite, Halt, HasExp, IsCOP0, isJAL, IsRet, IsShamt, MemtoReg,
       multiplexer_4_out, not_2_out, not_3_out, not_4_out, or_1_out, undriven_2;
  wire [31:0] adder_1_out, multiplexer_1_out, multiplexer_3_out, multiplexer_6_out, multiplexer_7_out,
       multiplexer_8_out, multiplexer_9_out, ram_1_dout, register_2_q, undriven, undriven_3, undriven_4;

  Multiplexer #(.width(32)) multiplexer_1 (.in1(undriven), .out(multiplexer_1_out), .sel(and_1_out));  // open: in0
  and and_1 (and_1_out, IsRet, IsCOP0);
  Multiplexer multiplexer_2 (.in0(clock_1_out), .in1(1'b0), .out(Clk), .sel(Halt));
  Clock clock_1 (.out(clock_1_out));
  Multiplexer #(.width(32)) multiplexer_3 (
    .in0({32{1'b0}}), .in1(multiplexer_1_out), .out(multiplexer_3_out), .sel(HasExp));
  not not_1 (HasExp, undriven_2);
  or or_1 (or_1_out, undriven_2, and_1_out);
  Register #(.width(32)) register_1 (.D(multiplexer_3_out), .clk(multiplexer_4_out));  // open: en, Q, clr
  Multiplexer multiplexer_4 (.in0(Clk), .in1(not_2_out), .out(multiplexer_4_out), .sel(or_1_out));
  not not_2 (not_2_out, Clk);
  // control_unit control_unit_1: pin names not known
  Adder #(.width(32)) adder_1 (.b({32{1'b0}}), .out(adder_1_out));  // open: a, cin, cout
  Register #(.width(32)) register_2 (.Q(register_2_q), .clk(HasExp));  // open: D, en, clr
  // CP0 cp0_1: pin names not known; wires that end beside it: Clk, HasExp, ExRegWrite
  Multiplexer #(.width(32)) multiplexer_5 (.in0(undriven_3), .in1(multiplexer_6_out), .sel(not_3_out));  // open: out
  not not_3 (not_3_out, IsCOP0);
  not not_4 (not_4_out, isJAL);
  Multiplexer #(.width(32)) multiplexer_6 (
    .in0(adder_1_out), .in1(multiplexer_9_out), .out(multiplexer_6_out), .sel(not_4_out));
  Multiplexer #(.width(32)) multiplexer_7 (.out(multiplexer_7_out), .sel(IsShamt));  // open: in0, in1
  Multiplexer #(.width(32)) multiplexer_8 (.out(multiplexer_8_out), .sel(IsShamt));  // open: in0, in1
  // alu alu_1: pin names not known; wires that end beside it: multiplexer_8_out
  RAM #(.dataWidth(32)) ram_1 (.addr(undriven_4[7:0]), .dout(ram_1_dout));  // open: we, oe, clk, din
  Multiplexer #(.width(32)) multiplexer_9 (.in0(undriven_4), .in1(ram_1_dout), .out(multiplexer_9_out), .sel(MemtoReg));
  // Pins of 8 and 32 bits meet at undriven_4

  // Notes on the sheet:
  //   PC Buffer
endmodule
